# Fritzing sketch button (saved by Fritzing 0.9.3b)
breadboards: 1

parts:
  Nano1 = Arduino Nano v2.3
  S1 = Round Pushbutton
  LED1 = LED - 5mm [color="Red (633nm)" package="5 mm [THT]"]
  U1 = RF-LINK_TX [package=rf-link_tx]
  J1 = Piezo Speaker
  VCC1 = 4 x AAA Battery Mount
  LED2 = LED - 5mm [color="Red (633nm)" package="5 mm [THT]"]
  LED3 = LED - 5mm [color="Green (560nm)" package="5 mm [THT]"]
  R1 = Resistor [tolerance=±5% resistance=330 package="2512 [SMD]"]
  R2 = Resistor [tolerance=±5% resistance=330 package="2512 [SMD]"]
  U2 = SWITCH_SPDT [package=kps-1290]

nets:
  GND: Nano1.GND, S1.leg1, LED1.anode, U1.GND, J1.pin1, VCC1.-, LED2.cathode, LED3.cathode
  N1: Nano1.D3, LED1.cathode
  N2: Nano1.D5, S1.leg0
  N3: Nano1.D9, R1.Pin_1
  N4: Nano1.D10, R2.Pin_1
  N5: Nano1.D12, U1.DATA
  N6: Nano1.D13, J1.pin2
  +5V: Nano1.+5V, U1.+5V
  N7: Nano1.VIN, U2.S
  N8: VCC1.+, U2.O
  N9: LED2.anode, R2.Pin_0
  N10: LED3.anode, R1.Pin_0

notes:
  I used the adfurit trinket pro 5V. not the arduino nano, but it is wired in the same port numbers. The nano vin port is BAT port on the trinket
  piezo buzzer
  The led is the one in the button
  This is the RF transmitter. Here are the ports:
  1 - ground
  2 - Data Input
  3 - VCC
  4 - Antenna (may not be a pin on the chip)(not essential)
